# Fritzing sketch breadboard (saved by Fritzing 0.9.6b)
breadboards: 1

parts:
  Part1 = 9-DOF Absolute Orientation IMU Fusion Breakout - BNO055  # not connected
  J1 = T Cobbler Plus
  MCU1 = Raspberry Pi Zero
  Power_Button = Momentary Switch [package=ksa_sealed_tac_switch]
  S4 = Momentary Switch [package=ksa_sealed_tac_switch]
  S5 = Momentary Switch [package=ksa_sealed_tac_switch]
  Part2 = Adafruit 128x32 Pi OLED [part_number="Adafruit #3527"]
  Part3 = Adafruit PowerBoost 1000C with USB Port [part_number="Adafruit #2465"]  # not connected
  R1 = Resistor [tolerance=±5% resistance=220 package="0603 [SMD]"]

nets:
  N1: J1.3.3V, MCU1.pin_1, MCU1.pin_17
  N2: J1.5V, MCU1.pin_2, MCU1.pin_4
  N3: J1.GPIO_2, MCU1.pin_3
  N4: J1.GPIO_3, MCU1.pin_5
  N5: J1.GND, MCU1.pin_6, MCU1.pin_9, MCU1.pin_14, MCU1.pin_20, MCU1.pin_25, MCU1.pin_30, MCU1.pin_34, MCU1.pin_39
  N6: J1.GPIO_4, MCU1.pin_7
  N7: J1.GPIO_14, MCU1.pin_8
  N8: J1.GPIO_15, MCU1.pin_10
  N9: J1.GPIO_17, MCU1.pin_11
  N10: J1.GPIO_18, MCU1.pin_12
  N11: J1.GPIO_27, MCU1.pin_13
  N12: J1.GPIO_22, MCU1.pin_15
  N13: J1.GPIO_23, MCU1.pin_16
  N14: J1.GPIO_24, MCU1.pin_18
  N15: J1.GPIO_10, MCU1.pin_19
  N16: J1.GPIO_9, MCU1.pin_21
  N17: J1.GPIO_25, MCU1.pin_22
  N18: J1.GPIO_11, MCU1.pin_23
  N19: J1.GPIO_8, MCU1.pin_24
  N20: J1.GPIO_7, MCU1.pin_26
  N21: J1.ID_SD, MCU1.pin_27
  N22: J1.ID_SC, MCU1.pin_28
  N23: J1.GPIO_5, MCU1.pin_29
  N24: J1.GPIO_6, MCU1.pin_31
  N25: J1.GPIO_12, MCU1.pin_32
  N26: J1.GPIO_13, MCU1.pin_33
  N27: J1.GPIO_19, MCU1.pin_35
  N28: J1.GPIO_16, MCU1.pin_36
  N29: J1.GPIO_26, MCU1.pin_37
  N30: J1.GPIO_20, MCU1.pin_38
  N31: J1.GPIO_21, MCU1.pin_40
  N32: Power_Button.4, Part2.SCL
  N33: S4.1, S5.1, R1.Pin_0
  N34: Part2.+5V, R1.Pin_1

custom parts:
  9-DOF Absolute Orientation IMU Fusion Breakout - BNO055: A MEMS accelerometer, magnetometer and gyroscope on a single die with a high speed ARM Cortex-M0 based processor to digest all the sensor data, abstract the sensor fusion and real time requirements away, and spit out data you can use in quaternions, Euler angles or vectors.
  T Cobbler Plus: The T-Cobbler Plus is an add on prototyping board from Adafruit specifically designed for the Raspberry Pi B+ that can break out all those tasty power, GPIO, I2C and SPI pins from the 40-pin header onto a solderless breadboard. This set will make "cobbling together" prototypes with the Pi super easy. The T-Cobbler Plus can plug into any solderless breadboard.
  Adafruit 128x32 Pi OLED: If you're looking for the most compact li'l display for a Raspberry Pi (most likely a Pi Zero) project, this might be just the thing you need! The Adafruit 128x32 PiOLED is your little OLED pal, ready to snap onto any and all Raspberry Pi computers, to give you a little display. The PiOLED comes with a monochrome 128x32 OLED, with sharp white pixels. The OLED uses only the I2C pins so you have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
  Adafruit PowerBoost 1000C with USB Port: PowerBoost 1000C is the perfect power supply for your portable project! With a built-in load-sharing battery charger circuit, you'll be able to keep your power-hungry project running even while recharging the battery! This little DC/DC boost converter module can be powered by any 3.7V LiIon/LiPoly battery, and convert the battery output to 5.2V DC for running your 5V projects.
